// Logisim project Aufgabe 3.circ as structural Verilog: 1 circuit, main circuit main
module main (
  input  A,
  input  R,
  input  S,
  input  in_4,
  input  in_5,
  output W,
  output out_7
);

  wire and_2_out, nand_2_out, nand_3_out, nand_4_out;

  and and_1 (S, ~A, ~R);  // AND_Gate
  buf and_2 (and_2_out, R);  // AND_Gate
  nand nand_1 (W, ~S, ~and_2_out);  // NAND_Gate
  nand nand_2 (nand_2_out, in_4, in_5);
  nand nand_3 (nand_3_out, in_4, nand_2_out);
  nand nand_4 (nand_4_out, nand_2_out, in_5);
  nand nand_5 (out_7, nand_3_out, nand_4_out);

  // Notes on the sheet:
  //   3. AUFGABE
  //   4. AUFGABE
endmodule
