// Logisim project Aufgabe 3 und 4.circ as structural Verilog: 1 circuit, main circuit main
module main (
  input  S,
  input  A,
  input  R,
  input  A_2,
  input  R_2,
  input  S_2,
  input  in_7,
  input  in_8,
  output W,
  output out_10,
  output out_11,
  output out_12
);

  wire and_2_out, and_3_out, and_4_out, and_5_out, and_6_out, and_7_out, nand_1_out, nand_3_out, nand_4_out;

  nand nand_1 (nand_1_out, in_7, in_8);
  and and_1 (S_2, ~A_2, ~R_2);  // AND_Gate
  buf and_2 (and_2_out, R_2);  // AND_Gate
  nand nand_2 (W, ~S_2, ~and_2_out);  // NAND_Gate
  nand nand_3 (nand_3_out, in_7, nand_1_out);
  nand nand_4 (nand_4_out, nand_1_out, in_8);
  nand nand_5 (out_12, nand_3_out, nand_4_out);
  and and_3 (and_3_out, ~S, ~A, R);  // AND_Gate
  and and_4 (and_4_out, ~S, A, R);  // AND_Gate
  and and_5 (and_5_out, S, ~A, ~R);  // AND_Gate
  and and_6 (and_6_out, ~S, R);  // AND_Gate
  and and_7 (and_7_out, S, ~A, ~R);  // AND_Gate
  or or_1 (out_10, and_3_out, and_4_out, and_5_out);
  or or_2 (out_11, and_6_out, and_7_out);

  // Notes on the sheet:
  //   a
  //   3. AUFGABE
  //   4. AUFGABE
  //   3. AUFGABE Lsg.
endmodule
